// Digital circuit 8BitSum.dig as structural Verilog
module _8BitSum (
  input  b0,
  input  b1,
  input  b2,
  input  b3,
  input  b4,
  input  b5,
  input  b6,
  input  b7,
  output s_0,
  output s_1,
  output s_2,
  output s_3
);

  wire and_1_out, and_2_out, and_3_out, and_4_out, and_5_out, and_6_out, and_7_out, and_8_out, and_9_out,
       and_10_out, and_12_out, and_13_out, and_14_out, and_15_out, xor_1_out, xor_2_out, xor_3_out,
       xor_4_out, xor_5_out, xor_6_out, xor_7_out, xor_8_out, xor_10_out, xor_11_out, xor_12_out, xor_13_out,
       xor_14_out, xor_15_out;

  xor xor_1 (xor_1_out, b0, b1);
  and and_1 (and_1_out, b1, b0);
  xor xor_2 (xor_2_out, b2, b3);
  and and_2 (and_2_out, b3, b2);
  xor xor_3 (xor_3_out, b4, b5);
  and and_3 (and_3_out, b5, b4);
  xor xor_4 (xor_4_out, b6, b7);
  and and_4 (and_4_out, b7, b6);
  xor xor_5 (xor_5_out, xor_1_out, xor_2_out);
  and and_5 (and_5_out, xor_1_out, xor_2_out);
  xor xor_6 (xor_6_out, and_1_out, and_2_out);
  and and_6 (and_6_out, and_1_out, and_2_out);
  xor xor_7 (xor_7_out, xor_3_out, xor_4_out);
  and and_7 (and_7_out, xor_3_out, xor_4_out);
  xor xor_8 (xor_8_out, and_3_out, and_4_out);
  and and_8 (and_8_out, and_3_out, and_4_out);
  xor xor_9 (s_0, xor_5_out, xor_7_out);
  and and_9 (and_9_out, xor_5_out, xor_7_out);
  xor xor_10 (xor_10_out, and_5_out, xor_6_out);
  and and_10 (and_10_out, and_5_out, xor_6_out);
  xor xor_11 (xor_11_out, and_6_out, and_8_out);
  and and_11 (s_3, and_6_out, and_8_out);
  xor xor_12 (xor_12_out, and_7_out, xor_8_out);
  and and_12 (and_12_out, xor_8_out, and_7_out);
  and and_13 (and_13_out, and_9_out, xor_10_out);
  xor xor_13 (xor_13_out, and_9_out, xor_10_out);
  and and_14 (and_14_out, and_13_out, and_10_out);
  xor xor_14 (xor_14_out, and_13_out, and_10_out);
  and and_15 (and_15_out, xor_13_out, xor_12_out);
  xor xor_15 (xor_15_out, xor_11_out, and_12_out);
  xor xor_16 (s_1, xor_13_out, xor_12_out);
  xor xor_17 (s_2, and_14_out, xor_14_out, and_15_out, xor_15_out);

  // Notes on the sheet:
  //   b_0
  //   b_1
  //   b_2
  //   b_3
endmodule
