// Digital circuit ConwayNextState.dig as structural Verilog
module ConwayNextState (
  input  [7:0] NBRS,
  input  STATE,
  output NEXT
);

  wire and_1_out, or_1_out;
  wire [3:0] bitcount_1_out;

  BitCount #(.Bits(8)) bitcount_1 (.in(NBRS), .out(bitcount_1_out));
  or or_1 (or_1_out, STATE, bitcount_1_out[0]);
  and and_1 (and_1_out, or_1_out, bitcount_1_out[1], ~bitcount_1_out[2], ~bitcount_1_out[3]);  // And
  xor xor_1 (NEXT, STATE, and_1_out);
endmodule
